// Logisim project HW6.circ as structural Verilog: 6 circuits, main circuit main
module main (
  input  in_1,
  input  in_2,
  input  in_3,
  input  in_4,
  input  in_5,
  input  in_6,
  input  in_7,
  input  in_8,
  output out_9,
  output out_10,
  output out_11,
  output out_12
);

  and and_1 (out_9, in_1, in_2);
  and and_2 (out_10, in_3, in_4);
  and and_3 (out_11, in_5, in_6);
  and and_4 (out_12, in_7, in_8);
endmodule

module half_adder (
  input  A,
  input  B,
  output out_3,
  output out_4
);

  and and_1 (out_3, A, B);
  xor xor_1 (out_4, B, A);

  // Notes on the sheet:
  //   Carry out
  //   Sum
endmodule

module full_adder (
  input  a,
  input  b,
  input  carry_in,
  output out_4,
  output carry_out
);

  wire half_adder_1_out_3, half_adder_1_out_4, half_adder_2_out_3;

  or or_1 (carry_out, half_adder_1_out_3, half_adder_2_out_3);
  half_adder half_adder_1 (.A(a), .B(b), .out_3(half_adder_1_out_3), .out_4(half_adder_1_out_4));
  half_adder half_adder_2 (.A(half_adder_1_out_4), .B(carry_in), .out_3(half_adder_2_out_3), .out_4(out_4));

  // Notes on the sheet:
  //   HA
  //   HA
  //   sum
endmodule

module ripple_adder (
  input  A0,
  input  B0,
  input  A1,
  input  B1,
  input  A2,
  input  B2,
  input  A3,
  input  B3,
  output S0,
  output S1,
  output S2,
  output Carry_out,
  output S3
);

  wire full_adder_2_carry_out, full_adder_3_carry_out, half_adder_1_out_3;

  full_adder full_adder_1 (.a(A3), .b(B3), .carry_out(Carry_out), .out_4(S3), .carry_in(full_adder_2_carry_out));
  full_adder full_adder_2 (
    .a(A2), .b(B2), .carry_out(full_adder_2_carry_out), .out_4(S2), .carry_in(full_adder_3_carry_out));
  full_adder full_adder_3 (
    .a(A1), .b(B1), .carry_out(full_adder_3_carry_out), .out_4(S1), .carry_in(half_adder_1_out_3));
  half_adder half_adder_1 (.A(A0), .B(B0), .out_3(half_adder_1_out_3), .out_4(S0));

  // Notes on the sheet:
  //   FA
  //   FA
  //   FA
  //   HA
endmodule

module HW6_q1 (
  input  A,
  input  B,
  input  C,
  input  D,
  output Out
);

  wire and_1_out, and_2_out, and_3_out, and_4_out, not_1_out, not_2_out, not_3_out, not_4_out, not_5_out,
       or_1_out, or_2_out;

  not not_1 (not_1_out, A);
  not not_2 (not_2_out, B);
  not not_3 (not_3_out, C);
  not not_4 (not_4_out, D);
  and and_1 (and_1_out, A, not_2_out);
  and and_2 (and_2_out, not_1_out, B);
  and and_3 (and_3_out, C, not_4_out);
  and and_4 (and_4_out, not_3_out, D);
  or or_1 (or_1_out, and_1_out, and_2_out);
  or or_2 (or_2_out, and_3_out, and_4_out);
  not not_5 (not_5_out, or_1_out);
  and and_5 (Out, not_5_out, or_2_out);
endmodule

module HW6_simple_alarm (
  input  System_on,
  input  Door,
  input  Floor,
  input  Window,
  output Alarm
);

  wire or_1_out;

  or or_1 (or_1_out, Door, Floor, Window);
  and and_1 (Alarm, or_1_out, System_on);
endmodule
